# Fritzing sketch Final circuit diagram (saved by Fritzing 1.0.2b)

parts:
  Part1 = Arduino Due (Rev2b)
  GY1 = MPU-6050 Board GY-521 [form="♀ (female)" package=THT]
  L298N1 = L298N DC motor driver
  L298N2 = L298N DC motor driver
  M1 = gear-motor
  M2 = gear-motor
  M3 = gear-motor
  M4 = gear-motor
  M5 = gear-motor
  M6 = gear-motor
  L298N3 = L298N DC motor driver
  Part2 = 20A DC-DC Buck  # not connected
  BAT1 = Battery Holders [package=lipo-1100mAh]  # not connected
  Part3 = Bluetooth HC-05 Macho
  M7 = RioRand LM2596  # not connected
  J1 = Basic Servo
  J2 = Basic Servo
  J3 = Basic Servo
  J4 = Basic Servo
  Enc1 = shaft encoder
  Enc2 = shaft encoder

nets:
  N1: Part1.D14/TX3, Part3.RXD
  N2: Part1.D15/RX3, Part3.TXD
  VCC: Part1.5V, GY1.pin1, Part3.VCC, Enc1.VCC
  GND: Part1.GND, GY1.pin2, L298N3.GND, Part3.GND, Enc1.GND, Enc2.GND
  VIN: Part1.VIN, L298N3.5V, Enc2.VCC
  N3: Part1.D8_PWM, J3.pulse
  N4: Part1.D9_PWM, J4.pulse
  N5: Part1.D10_PWM/SS0, J1.pulse
  N6: Part1.D11_PWM, J2.pulse
  N7: Part1.D13_PWM, GY1.pin8
  N8: Part1.SDA1, GY1.pin4
  N9: Part1.SCL1, GY1.pin3
  N10: Part1.D2_PWM, L298N1.ENA
  N11: Part1.D3_PWM, L298N1.ENB
  N12: Part1.D4_PWM/SS1, L298N3.ENA
  N13: Part1.D5_PWM, L298N3.ENB
  N14: Part1.D6_PWM, L298N2.ENA
  N15: Part1.D7_PWM, L298N2.ENB
  N16: Part1.D22, L298N3.IN4
  N17: Part1.D23, L298N2.IN1
  N18: Part1.D24, L298N3.IN3
  N19: Part1.D25, L298N2.IN2
  N20: Part1.D26, L298N3.IN2
  N21: Part1.D27, L298N2.IN3
  N22: Part1.D28, L298N3.IN1
  N23: Part1.D29, L298N2.IN4
  N24: Part1.D30, L298N1.IN4
  N25: Part1.D32, L298N1.IN3
  N26: Part1.D34, L298N1.IN2
  N27: Part1.D36, L298N1.IN1
  N28: Part1.D38, Enc2.OUT
  N29: Part1.D40, Enc1.OUT
  N30: L298N1.OUT1, M5.pin_2
  N31: L298N1.OUT2, M5.pin_1
  N32: L298N1.OUT3, M6.pin_2
  N33: L298N1.OUT4, M6.pin_1
  N34: L298N2.OUT1, M3.pin_2
  N35: L298N2.OUT2, M3.pin_1
  N36: L298N2.OUT3, M2.pin_2
  N37: L298N2.OUT4, M2.pin_1
  N38: M1.pin_1, L298N3.OUT4
  N39: M1.pin_2, L298N3.OUT3
  N40: M4.pin_1, L298N3.OUT2
  N41: M4.pin_2, L298N3.OUT1

custom parts:
  MPU-6050 Board GY-521: Acelerometro y Giroscopio MPU-6050 Board GY-521
  L298N DC motor driver: 2x DC motor driver with 78M05 positive voltage regulator (7..35 V) L298N: max 46 V, 2 A Set 5 V Enable jumper to enable 5 V regultor (needed for the L298N) and +5 V output at screw terminal or supply external +5 V at screw terminal Set ENA and/or ENB to +5 V to enable motor permanently or supply ENA and/or ENB with PWM signal IN1 and IN2 set rotation directory for motor A (OUT1/OUT2) IN2 and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
